// Logisim project single-cycle.circ as structural Verilog: 5 circuits, main circuit main
module alu (
  input  [31:0] A,
  input  [31:0] B,
  input  [3:0] ALUControl,
  input  [4:0] shamt,
  output Zero,
  output [31:0] R
);

  wire comparator_1_lt;
  wire [31:0] adder_1_out, and_1_out, bit_extender_1_out, nor_1_out, or_1_out, shifter_1_out,
       subtractor_1_out;

  assign and_1_out = A & B;  // AND_Gate and_1, 32 bits wide
  assign or_1_out = A | B;  // OR_Gate or_1, 32 bits wide
  Adder #(.width(32)) adder_1 (.a(A), .b(B), .out(adder_1_out));  // open: cin, cout
  Subtractor #(.width(32)) subtractor_1 (.a(A), .b(B), .out(subtractor_1_out));  // open: bin, bout
  Comparator #(.width(32)) comparator_1 (.a(A), .b(B), .lt(comparator_1_lt));  // open: gt, eq
  assign nor_1_out = ~(A | B);  // NOR_Gate nor_1, 32 bits wide
  assign bit_extender_1_out = {{31{comparator_1_lt}}, comparator_1_lt};  // Bit_Extender bit_extender_1
  Shifter #(.width(32)) shifter_1 (.in(A), .\dist (shamt), .out(shifter_1_out));
  Multiplexer #(.select(4), .width(32)) multiplexer_1 (
    .in0(and_1_out), .in1(or_1_out), .in2(adder_1_out), .in6(subtractor_1_out), .in7(bit_extender_1_out),
    .in12(nor_1_out), .in15(shifter_1_out), .out(R), .sel(ALUControl));  // open: in3, in4, in5, in8, in9, in10, in11, in13, in14
  Comparator #(.width(32)) comparator_2 (.a({32{1'b0}}), .b(R), .eq(Zero));  // open: gt, lt
endmodule

module main (
);

  wire ALUSrc, and_1_out, Branch, clock_1_out, clock_2_out, clock_3_out, Jump, JumpReg, MemRead, MemToReg,
       MemWrite, PCto31, RegDst, RegWrite, Zero;
  wire [1:0] ALUOp;
  wire [3:0] aluctrl_1_alucontrol;
  wire [4:0] multiplexer_1_out, multiplexer_2_out;
  wire [7:0] IM_p2, IM_p3, IM_p4, IM_p5, undriven, undriven_2, undriven_3, undriven_4;
  wire [23:0] PC_q;
  wire [31:0] adder_2_out, alu_1_r, bit_extender_1_out, controlled_buffer_1_out, D1, multiplexer_3_out,
       multiplexer_4_out, multiplexer_5_out, multiplexer_7_out, PCmas4, PCNext, registers_1_d2,
       shifter_1_out, WD;
  wire [31:24] PC_q_2;

  Register #(.width(32)) PC (.D(PCNext), .clk(clock_1_out), .Q({PC_q_2, PC_q}));  // open: en, clr
  Clock clock_1 (.out(clock_1_out));
  Adder #(.width(32)) adder_1 (.a(32'h4), .b({PC_q_2, PC_q}), .out(PCmas4));  // open: cin, cout
  // ROM #(.addrWidth(24), .line("quad")) IM: pin names not known; wires that end beside it: PC_q, IM_p2, IM_p3, IM_p4, IM_p5
  Multiplexer #(.width(5)) multiplexer_1 (.in0(IM_p3[4:0]), .in1(IM_p4[7:3]), .out(multiplexer_1_out), .sel(RegDst));
  Multiplexer #(.width(5)) multiplexer_2 (
    .in0(multiplexer_1_out), .in1({5{1'b1}}), .out(multiplexer_2_out), .sel(PCto31));
  Clock clock_2 (.out(clock_2_out));
  Multiplexer #(.width(32)) multiplexer_3 (.in0(WD), .in1(PCmas4), .out(multiplexer_3_out), .sel(PCto31));
  assign bit_extender_1_out = {{16{IM_p4[7]}}, {IM_p4, IM_p5}};  // Bit_Extender bit_extender_1
  control control_1 (
    .opcode(IM_p2[7:2]), .ALUSrc(ALUSrc), .RegDst(RegDst), .MemToReg(MemToReg), .Jump(Jump), .Branch(Branch),
    .RegWrite(RegWrite), .MemRead(MemRead), .MemWrite(MemWrite), .ALUOp(ALUOp), .PCto31(PCto31));
  registers registers_1 (
    .R1({IM_p2[1:0], IM_p3[7:5]}), .R2(IM_p3[4:0]), .WR(multiplexer_2_out), .WD(multiplexer_3_out),
    .CLK(clock_2_out), .RegWrite(RegWrite), .D1(D1), .D2(registers_1_d2));
  Multiplexer #(.width(32)) multiplexer_4 (
    .in0(multiplexer_7_out), .in1({PCmas4[31:28], IM_p2[1:0], IM_p3, IM_p4, IM_p5, 2'b00}),
    .out(multiplexer_4_out), .sel(Jump));
  aluctrl aluctrl_1 (.funct(IM_p5[5:0]), .ALUOp(ALUOp), .JumpReg(JumpReg), .ALUControl(aluctrl_1_alucontrol));
  Shifter #(.width(32)) shifter_1 (.in(bit_extender_1_out), .\dist (5'b00010), .out(shifter_1_out));
  Multiplexer #(.width(32)) multiplexer_5 (
    .in0(registers_1_d2), .in1(bit_extender_1_out), .out(multiplexer_5_out), .sel(ALUSrc));
  Multiplexer #(.width(32)) multiplexer_6 (.in0(multiplexer_4_out), .in1(D1), .out(PCNext), .sel(JumpReg));
  Adder #(.width(32)) adder_2 (.a({PC_q_2, PC_q}), .b(shifter_1_out), .out(adder_2_out));  // open: cin, cout
  Multiplexer #(.width(32)) multiplexer_7 (.in0(PCmas4), .in1(adder_2_out), .out(multiplexer_7_out), .sel(and_1_out));
  and and_1 (and_1_out, Branch, Zero);
  alu alu_1 (
    .A(D1), .B(multiplexer_5_out), .ALUControl(aluctrl_1_alucontrol), .shamt({IM_p4[2:0], IM_p5[7:6]}),
    .Zero(Zero), .R(alu_1_r));
  Clock clock_3 (.out(clock_3_out));
  // RAM #(.addrWidth(24), .enables("line"), .line("quad")) DM: pin names not known; wires that end beside it: alu_1_r[23:0], MemWrite, clock_3_out
  assign controlled_buffer_1_out = MemRead ? {undriven_4, undriven_3, undriven_2, undriven} : 32'bz;  // Controlled_Buffer controlled_buffer_1
  Multiplexer #(.width(32)) multiplexer_8 (.in0(alu_1_r), .in1(controlled_buffer_1_out), .out(WD), .sel(MemToReg));

  // Notes on the sheet:
  //   PC + 4
  //   contents of IM (hex, n*v repeats v):
  //   c 0 0 10 34 8 0 10 8*0 34 8 0 0 1 0 0 8 40*0 3 e0 0 8
  //   PC + 4
  //   PC
  //   bits [31:28] de PC+4
  //   addr
  //   addr
  //   rs
  //   rt
  //   rt (I)
  //   rd (R)
  //   imm
  //   ($ra)
  //   Si es 1, guarda la sig. inst. en $ra
  //   Jump Target (31:28(PC+4) - addr - 00)
  //   PC + 4
  //   PC
  //   Habilita la escritura en el RegFile
  //   shamt
  //   S. EXT shift 2 + PC
  //   para "jr"
  //   Branch Target
  //   Zero de ALU(reg. iguales) y Branch activo
  //   PC+4 o Branch
  //   Habilita la escritura
  //   de memoria
  //   Habilita la lectura de memoria
  //   R de ALU a WD si vale 0 (R)
  //   DM a WD si vale 1  (lw)
  //   Escribe en el RegFile
endmodule

module registers (
  input  [4:0] R1,
  input  [4:0] R2,
  input  [4:0] WR,
  input  [31:0] WD,
  input  CLK,
  input  RegWrite,
  output [31:0] D1,
  output [31:0] D2
);

  wire WE1, WE2, WE3, WE4, WE5, WE6, WE7, WE8, WE9, WE10, WE11, WE12, WE13, WE14, WE15, WE16, WE17, WE18,
       WE19, WE20, WE21, WE22, WE23, WE24, WE25, WE26, WE27, WE28, WE29, WE30, WE31;
  wire [31:0] Q0, Q1, Q2, Q3, Q4, Q5, Q6, Q7, Q8, Q9, Q10, Q11, Q12, Q13, Q14, Q15, Q16, Q17, Q18, Q19, Q20,
       Q21, Q22, Q23, Q24, Q25, Q26, Q27, Q28, Q29, Q30, Q31;

  Demultiplexer #(.select(5)) demultiplexer_1 (
    .out1(WE1), .out2(WE2), .out3(WE3), .out4(WE4), .out5(WE5), .out6(WE6), .out7(WE7), .out8(WE8),
    .out9(WE9), .out10(WE10), .out11(WE11), .out12(WE12), .out13(WE13), .out14(WE14), .out15(WE15),
    .out16(WE16), .out17(WE17), .out18(WE18), .out19(WE19), .out20(WE20), .out21(WE21), .out22(WE22),
    .out23(WE23), .out24(WE24), .out25(WE25), .out26(WE26), .out27(WE27), .out28(WE28), .out29(WE29),
    .out30(WE30), .out31(WE31), .in(RegWrite), .sel(WR));  // open: out0
  Register #(.width(32)) zero (.D({32{1'b0}}), .clk(CLK), .Q(Q0));  // open: en, clr
  Register #(.width(32)) a0 (.D(WD), .en(WE4), .clk(CLK), .Q(Q4));  // open: clr
  Register #(.width(32)) t0 (.D(WD), .en(WE8), .clk(CLK), .Q(Q8));  // open: clr
  Register #(.width(32)) t4 (.D(WD), .en(WE12), .clk(CLK), .Q(Q12));  // open: clr
  Register #(.width(32)) s0 (.D(WD), .en(WE16), .clk(CLK), .Q(Q16));  // open: clr
  Register #(.width(32)) s4 (.D(WD), .en(WE20), .clk(CLK), .Q(Q20));  // open: clr
  Register #(.width(32)) t8 (.D(WD), .en(WE24), .clk(CLK), .Q(Q24));  // open: clr
  Register #(.width(32)) gp (.D(WD), .en(WE28), .clk(CLK), .Q(Q28));  // open: clr
  Register #(.width(32)) at (.D(WD), .en(WE1), .clk(CLK), .Q(Q1));  // open: clr
  Register #(.width(32)) a1 (.D(WD), .en(WE5), .clk(CLK), .Q(Q5));  // open: clr
  Register #(.width(32)) t1 (.D(WD), .en(WE9), .clk(CLK), .Q(Q9));  // open: clr
  Register #(.width(32)) t5 (.D(WD), .en(WE13), .clk(CLK), .Q(Q13));  // open: clr
  Register #(.width(32)) s1 (.D(WD), .en(WE17), .clk(CLK), .Q(Q17));  // open: clr
  Register #(.width(32)) s5 (.D(WD), .en(WE21), .clk(CLK), .Q(Q21));  // open: clr
  Register #(.width(32)) t9 (.D(WD), .en(WE25), .clk(CLK), .Q(Q25));  // open: clr
  Register #(.width(32)) sp (.D(WD), .en(WE29), .clk(CLK), .Q(Q29));  // open: clr
  Register #(.width(32)) v0 (.D(WD), .en(WE2), .clk(CLK), .Q(Q2));  // open: clr
  Register #(.width(32)) a2 (.D(WD), .en(WE6), .clk(CLK), .Q(Q6));  // open: clr
  Register #(.width(32)) t2 (.D(WD), .en(WE10), .clk(CLK), .Q(Q10));  // open: clr
  Register #(.width(32)) t6 (.D(WD), .en(WE14), .clk(CLK), .Q(Q14));  // open: clr
  Register #(.width(32)) s2 (.D(WD), .en(WE18), .clk(CLK), .Q(Q18));  // open: clr
  Register #(.width(32)) s6 (.D(WD), .en(WE22), .clk(CLK), .Q(Q22));  // open: clr
  Register #(.width(32)) k0 (.D(WD), .en(WE26), .clk(CLK), .Q(Q26));  // open: clr
  Register #(.width(32)) fp (.D(WD), .en(WE30), .clk(CLK), .Q(Q30));  // open: clr
  Register #(.width(32)) v1 (.D(WD), .en(WE3), .clk(CLK), .Q(Q3));  // open: clr
  Register #(.width(32)) a3 (.D(WD), .en(WE7), .clk(CLK), .Q(Q7));  // open: clr
  Register #(.width(32)) t3 (.D(WD), .en(WE11), .clk(CLK), .Q(Q11));  // open: clr
  Register #(.width(32)) t7 (.D(WD), .en(WE15), .clk(CLK), .Q(Q15));  // open: clr
  Register #(.width(32)) s3 (.D(WD), .en(WE19), .clk(CLK), .Q(Q19));  // open: clr
  Register #(.width(32)) s7 (.D(WD), .en(WE23), .clk(CLK), .Q(Q23));  // open: clr
  Register #(.width(32)) k1 (.D(WD), .en(WE27), .clk(CLK), .Q(Q27));  // open: clr
  Register #(.width(32)) ra (.D(WD), .en(WE31), .clk(CLK), .Q(Q31));  // open: clr
  Multiplexer #(.select(5), .width(32)) multiplexer_1 (
    .in0(Q0), .in1(Q1), .in2(Q2), .in3(Q3), .in4(Q4), .in5(Q5), .in6(Q6), .in7(Q7), .in8(Q8), .in9(Q9),
    .in10(Q10), .in11(Q11), .in12(Q12), .in13(Q13), .in14(Q14), .in15(Q15), .in16(Q16), .in17(Q17),
    .in18(Q18), .in19(Q19), .in20(Q20), .in21(Q21), .in22(Q22), .in23(Q23), .in24(Q24), .in25(Q25),
    .in26(Q26), .in27(Q27), .in28(Q28), .in29(Q29), .in30(Q30), .in31(Q31), .out(D1), .sel(R1));
  Multiplexer #(.select(5), .width(32)) multiplexer_2 (
    .in0(Q0), .in1(Q1), .in2(Q2), .in3(Q3), .in4(Q4), .in5(Q5), .in6(Q6), .in7(Q7), .in8(Q8), .in9(Q9),
    .in10(Q10), .in11(Q11), .in12(Q12), .in13(Q13), .in14(Q14), .in15(Q15), .in16(Q16), .in17(Q17),
    .in18(Q18), .in19(Q19), .in20(Q20), .in21(Q21), .in22(Q22), .in23(Q23), .in24(Q24), .in25(Q25),
    .in26(Q26), .in27(Q27), .in28(Q28), .in29(Q29), .in30(Q30), .in31(Q31), .out(D2), .sel(R2));
endmodule

module control (
  input  [5:0] opcode,
  output ALUSrc,
  output RegDst,
  output MemToReg,
  output Jump,
  output Branch,
  output RegWrite,
  output MemRead,
  output MemWrite,
  output [1:0] ALUOp,
  output PCto31
);

  wire addi_out, j_out, ori_out;

  and R (RegDst, ~opcode[5], ~opcode[4], ~opcode[3], ~opcode[2], ~opcode[1], ~opcode[0]);  // AND_Gate
  and lw (MemRead, opcode[5], ~opcode[4], ~opcode[3], ~opcode[2], opcode[1], opcode[0]);  // AND_Gate
  and sw (MemWrite, opcode[5], ~opcode[4], opcode[3], ~opcode[2], opcode[1], opcode[0]);  // AND_Gate
  and beq (Branch, ~opcode[5], ~opcode[4], ~opcode[3], opcode[2], ~opcode[1], ~opcode[0]);  // AND_Gate
  and j (j_out, ~opcode[5], ~opcode[4], ~opcode[3], ~opcode[2], opcode[1], ~opcode[0]);  // AND_Gate
  and addi (addi_out, ~opcode[5], ~opcode[4], opcode[3], ~opcode[2], ~opcode[1], ~opcode[0]);  // AND_Gate
  and ori (ori_out, ~opcode[5], ~opcode[4], opcode[3], opcode[2], ~opcode[1], opcode[0]);  // AND_Gate
  and jal (PCto31, ~opcode[5], ~opcode[4], ~opcode[3], ~opcode[2], opcode[1], opcode[0]);  // AND_Gate
  or or_1 (ALUSrc, ori_out, addi_out, MemWrite, MemRead);
  or or_2 (Jump, PCto31, j_out);
  or or_3 (RegWrite, ori_out, addi_out, PCto31, MemRead, RegDst);
  or or_4 (ALUOp[0], ori_out, Branch);
  or or_5 (ALUOp[1], RegDst, ori_out);

  assign MemToReg = MemRead;
endmodule

module aluctrl (
  input  [5:0] funct,
  input  [1:0] ALUOp,
  output JumpReg,
  output [3:0] ALUControl
);

  wire [3:0] multiplexer_1_out, multiplexer_2_out;

  Multiplexer #(.select(4), .width(4)) multiplexer_1 (
    .in0(4'b0010), .in2(4'b0110), .in4(4'b0000), .in5(4'b0001), .in7(4'b1100), .in10(4'b0111),
    .out(multiplexer_1_out), .sel(funct[3:0]));  // open: in1, in3, in6, in8, in9, in11, in12, in13, in14, in15
  Multiplexer #(.width(4)) multiplexer_2 (
    .in0(4'b1111), .in1(multiplexer_1_out), .out(multiplexer_2_out), .sel(funct[5]));
  and and_1 (JumpReg, ~funct[0], ~funct[1], ~funct[2], funct[3]);  // AND_Gate
  Multiplexer #(.select(2), .width(4)) multiplexer_3 (
    .in0(4'b0010), .in1(4'b0110), .in2(multiplexer_2_out), .in3(4'b0001), .out(ALUControl), .sel(ALUOp));
endmodule
